# Fritzing sketch Soil_moisture_esp (saved by Fritzing 0.9.3b)
perfboards: 1

parts:
  J1 = female pin header, 4 pins [form="♀ (female)"]
  J2 = female pin header, 15 pins [form="♀ (female)"]
  J3 = female pin header, 15 pins [form="♀ (female)"]
  J4 = female pin header, 4 pins [form="♀ (female)"]
  J5 = female pin header, 4 pins [form="♀ (female)"]
  J6 = female pin header, 4 pins [form="♀ (female)"]
  J7 = female pin header, 4 pins [form="♀ (female)"]
  J8 = female pin header, 10 pins [form="♀ (female)"]
  Bauteil1 = ADS1115  # not connected
  U1 = NodeMCU V1.0

nets:
  N1: J1.pin1, J2.pin7, J2.pin14, J3.pin10, J3.pin14, J4.pin1, J5.pin1, J6.pin1, J7.pin1, J8.pin6, J8.pin9, U1.GND
  N2: J1.pin2, J2.pin6, J2.pin15, J3.pin11, J4.pin2, J5.pin2, J6.pin2, J7.pin2, U1.3V3
  N3: J1.pin4, J3.pin1, U1.A0
  N4: J2.pin1, U1.D0
  N5: J2.pin2, J8.pin8, U1.D1
  N6: J2.pin3, J8.pin7, U1.D2
  N7: J2.pin4, U1.D3
  N8: J2.pin5, U1.D4
  N9: J2.pin8, U1.D5
  N10: J2.pin9, U1.D6
  N11: J2.pin10, U1.D7
  N12: J2.pin11, U1.D8
  N13: J2.pin12, U1.RX
  N14: J2.pin13, U1.TX
  N15: J3.pin2, U1.RSV#41
  N16: J3.pin3, U1.RSV#40
  N17: J3.pin4, U1.SD3
  N18: J3.pin5, U1.SD2
  N19: J3.pin6, U1.SD1
  N20: J3.pin7, U1.CMD
  N21: J3.pin8, U1.SD0
  N22: J3.pin9, U1.CLK
  N23: J3.pin12, U1.EN
  N24: J3.pin13, U1.RST
  N25: J3.pin15, J8.pin10, U1.Vin
  N26: J4.pin4, J8.pin1
  N27: J5.pin4, J8.pin2
  N28: J6.pin4, J8.pin3
  N29: J7.pin4, J8.pin4

notes:
  Sensor 1
  Sensor 5
  Sensor 4
  Sensor 3
  Sensor 2

custom parts:
  ADS1115: ADC ADS1115
  NodeMCU V1.0: ESP8266 based NodeMCU
